# Fritzing sketch Untitled Sketch 2 (saved by Fritzing 0.9.4)
breadboards: 1

parts:
  S1 = Reed switch [package=THT]
  Part1 = Adafruit Metro with Headers [part_number="Adafruit #2488"]
  S2 = Momentary Switch [package=ksa_sealed_tac_switch]
  R2 = Resistor [tolerance=±5% resistance=100k package=THT]
  R3 = Resistor [tolerance=±5% resistance=100k package=THT]

nets:
  N1: S1.pin_1, Part1.IO2, R3.Pin_1
  N2: S1.pin_2, Part1.+5V, S2.4
  N3: Part1.GND, R2.Pin_1, R3.Pin_0
  N4: Part1.IO3, S2.2, R2.Pin_0

custom parts:
  Adafruit Metro with Headers: We sure love the ATmega328 here at Adafruit, and we use them a lot for our own projects. The processor has plenty of GPIO, Analog inputs, hardware UART SPI and I2C, timers and PWM galore - just enough for most simple projects. When we need to go small, we use a Pro Trinket 3V or 5V, but when size isn't as much of a concern, and an USB-serial converter is required, we reach for an Adafruit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
